// Logisim project Milestone1.circ as structural Verilog: 12 circuits, main circuit main
module main (
);

  wire alu_ctrl_1_alu_src, and_1_out, clock_1_out, comparator_1_eq, main_control_unit_1_branch,
       main_control_unit_1_memread, main_control_unit_1_memtoreg, main_control_unit_1_memwrite,
       main_control_unit_1_regwrite;
  wire [3:0] alu_ctrl_1_alu_ctrl0;
  wire [31:0] adder_1_out, adder_2_out, data_memory_1_read_data, immgen_1_imm32,
       instructional_memory_1_instruction, multiplexer_1_out, multiplexer_2_out, multiplexer_3_out,
       register_1_q, register_file_1_rdata1, register_file_1_rdata2, thirtytwo_bit_alu_1_r;

  Register #(.width(32)) register_1 (
    .D(multiplexer_2_out), .en(1'b1), .clk(clock_1_out), .Q(register_1_q));  // open: clr
  Clock clock_1 (.out(clock_1_out));
  Adder #(.width(32)) adder_1 (.a(register_1_q), .b(32'h4), .out(adder_1_out));  // open: cin, cout
  Instructional_Memory instructional_memory_1 (
    .Address(register_1_q[23:0]), .Clk_In(clock_1_out), .Instruction(instructional_memory_1_instruction));
  Main_Control_Unit main_control_unit_1 (
    .I6(instructional_memory_1_instruction[6]), .I5(instructional_memory_1_instruction[5]),
    .I4(instructional_memory_1_instruction[4]), .I3(instructional_memory_1_instruction[3]),
    .I2(instructional_memory_1_instruction[2]), .I1(instructional_memory_1_instruction[1]),
    .I0(instructional_memory_1_instruction[0]), .MemtoReg(main_control_unit_1_memtoreg),
    .RegWrite(main_control_unit_1_regwrite), .MemRead(main_control_unit_1_memread),
    .MemWrite(main_control_unit_1_memwrite), .Branch(main_control_unit_1_branch));
  Register_File register_file_1 (
    .RReg1(instructional_memory_1_instruction[19:15]), .WData(multiplexer_3_out), .Clock_in(clock_1_out),
    .Write(main_control_unit_1_regwrite), .WReg(instructional_memory_1_instruction[11:7]),
    .RReg2(instructional_memory_1_instruction[24:20]), .RData1(register_file_1_rdata1),
    .RData2(register_file_1_rdata2));
  ImmGen immgen_1 (.Instruction(instructional_memory_1_instruction), .IMM32(immgen_1_imm32));
  ALU_Ctrl alu_ctrl_1 (
    .I30(instructional_memory_1_instruction[30]), .I14(instructional_memory_1_instruction[14]),
    .I13(instructional_memory_1_instruction[13]), .I12(instructional_memory_1_instruction[12]),
    .I6(instructional_memory_1_instruction[6]), .I5(instructional_memory_1_instruction[5]),
    .I4(instructional_memory_1_instruction[4]), .ALU_Ctrl3(alu_ctrl_1_alu_ctrl0[3]),
    .ALU_Ctrl2(alu_ctrl_1_alu_ctrl0[2]), .ALU_Ctrl1(alu_ctrl_1_alu_ctrl0[1]),
    .ALU_Ctrl0(alu_ctrl_1_alu_ctrl0[0]), .ALU_Src(alu_ctrl_1_alu_src));
  Multiplexer #(.enable("false"), .width(32)) multiplexer_1 (
    .in0(register_file_1_rdata2), .in1(immgen_1_imm32), .out(multiplexer_1_out), .sel(alu_ctrl_1_alu_src));
  Comparator #(.width(32)) comparator_1 (
    .a(register_file_1_rdata1), .b(register_file_1_rdata2), .eq(comparator_1_eq));  // open: gt, lt
  and and_1 (and_1_out, main_control_unit_1_branch, comparator_1_eq);
  ThirtyTwo_Bit_ALU thirtytwo_bit_alu_1 (
    .ALU_Ctrl(alu_ctrl_1_alu_ctrl0), .A(register_file_1_rdata1), .B(multiplexer_1_out),
    .R(thirtytwo_bit_alu_1_r));  // open: C_out
  Adder #(.width(32)) adder_2 (.a(register_1_q), .b(immgen_1_imm32), .out(adder_2_out));  // open: cin, cout
  Multiplexer #(.enable("false"), .width(32)) multiplexer_2 (
    .in0(adder_1_out), .in1(adder_2_out), .out(multiplexer_2_out), .sel(and_1_out));
  Data_Memory data_memory_1 (
    .Address(thirtytwo_bit_alu_1_r[25:0]), .Mem_Write(main_control_unit_1_memwrite),
    .Mem_Read(main_control_unit_1_memread), .Clk_In(clock_1_out), .Write_Data(register_file_1_rdata2),
    .Read_Data(data_memory_1_read_data));
  Multiplexer #(.enable("false"), .width(32)) multiplexer_3 (
    .in0(thirtytwo_bit_alu_1_r), .in1(data_memory_1_read_data), .out(multiplexer_3_out),
    .sel(main_control_unit_1_memtoreg));
endmodule

module OneBitAdder (
  input  A,
  input  B,
  input  C_in,
  output S,
  output C_out
);

  wire and_1_out, and_2_out, and_3_out, and_4_out, and_5_out, and_6_out, and_7_out, not_1_out, not_2_out,
       not_3_out;

  not not_1 (not_1_out, A);
  not not_2 (not_2_out, B);
  not not_3 (not_3_out, C_in);
  and and_1 (and_1_out, not_1_out, not_2_out, C_in);
  and and_2 (and_2_out, not_1_out, B, not_3_out);
  and and_3 (and_3_out, A, not_2_out, not_3_out);
  and and_4 (and_4_out, A, B, C_in);
  and and_5 (and_5_out, B, C_in);
  and and_6 (and_6_out, A, C_in);
  and and_7 (and_7_out, A, B);
  or or_1 (S, and_1_out, and_2_out, and_3_out, and_4_out);
  or or_2 (C_out, and_5_out, and_6_out, and_7_out);
endmodule

module ALU_Ctrl (
  input  I30,
  input  I14,
  input  I13,
  input  I12,
  input  I6,
  input  I5,
  input  I4,
  output ALU_Ctrl3,
  output ALU_Ctrl2,
  output ALU_Ctrl1,
  output ALU_Ctrl0,
  output ALU_Src
);

  wire and_2_out, not_1_out, not_2_out, not_3_out, not_4_out, not_5_out;

  not not_1 (not_1_out, I14);
  not not_2 (not_2_out, I13);
  not not_3 (not_3_out, I12);
  not not_4 (not_4_out, I5);
  not not_5 (not_5_out, I4);
  and and_1 (ALU_Ctrl2, I30, not_2_out, I5);
  or or_1 (ALU_Ctrl1, not_2_out, not_5_out);
  and and_2 (and_2_out, I13, not_3_out);
  or or_2 (ALU_Src, not_4_out, not_5_out);
  or or_3 (ALU_Ctrl0, not_1_out, and_2_out);

  assign ALU_Ctrl3 = 1'b0;
endmodule

module One_Bit_ALU (
  input  [3:0] ALU_Ctrl_in,
  input  A,
  input  B,
  input  C_in,
  output R,
  output C_out
);

  wire and_1_out, multiplexer_1_out, not_1_out, onebitadder_1_s, or_1_out, xor_1_out;

  not not_1 (not_1_out, B);
  Multiplexer #(.enable("false")) multiplexer_1 (
    .in0(B), .in1(not_1_out), .out(multiplexer_1_out), .sel(ALU_Ctrl_in[2]));
  and and_1 (and_1_out, A, multiplexer_1_out);
  or or_1 (or_1_out, A, multiplexer_1_out);
  xor xor_1 (xor_1_out, A, multiplexer_1_out);
  OneBitAdder onebitadder_1 (.A(A), .B(multiplexer_1_out), .C_in(C_in), .S(onebitadder_1_s), .C_out(C_out));
  Multiplexer #(.enable("false"), .select(2)) multiplexer_2 (
    .in0(and_1_out), .in1(or_1_out), .in2(xor_1_out), .in3(onebitadder_1_s), .out(R), .sel(ALU_Ctrl_in[1:0]));
endmodule

module Four_Bit_ALU (
  input  [3:0] ALU_Ctrl,
  input  [3:0] A,
  input  C_in,
  input  [3:0] B,
  output [3:0] R,
  output C_out
);

  wire one_bit_alu_1_c_out, one_bit_alu_2_c_out, one_bit_alu_3_c_out;

  One_Bit_ALU one_bit_alu_1 (
    .ALU_Ctrl_in(ALU_Ctrl), .A(A[0]), .B(B[0]), .C_in(C_in), .R(R[0]), .C_out(one_bit_alu_1_c_out));
  One_Bit_ALU one_bit_alu_2 (
    .ALU_Ctrl_in(ALU_Ctrl), .A(A[1]), .B(B[1]), .C_in(one_bit_alu_1_c_out), .R(R[1]),
    .C_out(one_bit_alu_2_c_out));
  One_Bit_ALU one_bit_alu_3 (
    .ALU_Ctrl_in(ALU_Ctrl), .A(A[2]), .B(B[2]), .C_in(one_bit_alu_2_c_out), .R(R[2]),
    .C_out(one_bit_alu_3_c_out));
  One_Bit_ALU one_bit_alu_4 (
    .ALU_Ctrl_in(ALU_Ctrl), .A(A[3]), .B(B[3]), .C_in(one_bit_alu_3_c_out), .R(R[3]), .C_out(C_out));
endmodule

module ThirtyTwo_Bit_ALU (
  input  [3:0] ALU_Ctrl,
  input  [31:0] A,
  input  [31:0] B,
  output [31:0] R,
  output C_out
);

  wire four_bit_alu_1_c_out, four_bit_alu_2_c_out, four_bit_alu_3_c_out, four_bit_alu_4_c_out,
       four_bit_alu_5_c_out, four_bit_alu_6_c_out, four_bit_alu_7_c_out;

  Four_Bit_ALU four_bit_alu_1 (
    .ALU_Ctrl(ALU_Ctrl), .A(A[3:0]), .C_in(ALU_Ctrl[2]), .B(B[3:0]), .R(R[3:0]), .C_out(four_bit_alu_1_c_out));
  Four_Bit_ALU four_bit_alu_2 (
    .ALU_Ctrl(ALU_Ctrl), .A(A[7:4]), .C_in(four_bit_alu_1_c_out), .B(B[7:4]), .R(R[7:4]),
    .C_out(four_bit_alu_2_c_out));
  Four_Bit_ALU four_bit_alu_3 (
    .ALU_Ctrl(ALU_Ctrl), .A(A[11:8]), .C_in(four_bit_alu_2_c_out), .B(B[11:8]), .R(R[11:8]),
    .C_out(four_bit_alu_3_c_out));
  Four_Bit_ALU four_bit_alu_4 (
    .ALU_Ctrl(ALU_Ctrl), .A(A[15:12]), .C_in(four_bit_alu_3_c_out), .B(B[15:12]), .R(R[15:12]),
    .C_out(four_bit_alu_4_c_out));
  Four_Bit_ALU four_bit_alu_5 (
    .ALU_Ctrl(ALU_Ctrl), .A(A[19:16]), .C_in(four_bit_alu_4_c_out), .B(B[19:16]), .R(R[19:16]),
    .C_out(four_bit_alu_5_c_out));
  Four_Bit_ALU four_bit_alu_6 (
    .ALU_Ctrl(ALU_Ctrl), .A(A[23:20]), .C_in(four_bit_alu_5_c_out), .B(B[23:20]), .R(R[23:20]),
    .C_out(four_bit_alu_6_c_out));
  Four_Bit_ALU four_bit_alu_7 (
    .ALU_Ctrl(ALU_Ctrl), .A(A[27:24]), .C_in(four_bit_alu_6_c_out), .B(B[27:24]), .R(R[27:24]),
    .C_out(four_bit_alu_7_c_out));
  Four_Bit_ALU four_bit_alu_8 (
    .ALU_Ctrl(ALU_Ctrl), .A(A[31:28]), .C_in(four_bit_alu_7_c_out), .B(B[31:28]), .R(R[31:28]), .C_out(C_out));
endmodule

module Register_File (
  input  [4:0] RReg1,
  input  [31:0] WData,
  input  Clock_in,
  input  Write,
  input  [4:0] WReg,
  input  [4:0] RReg2,
  output [31:0] RData1,
  output [31:0] RData2
);

  wire demultiplexer_1_out0, demultiplexer_1_out1, demultiplexer_1_out2, demultiplexer_1_out3,
       demultiplexer_1_out4, demultiplexer_1_out5, demultiplexer_1_out6, demultiplexer_1_out7,
       demultiplexer_1_out8, demultiplexer_1_out9, demultiplexer_1_out21, demultiplexer_1_out22,
       demultiplexer_1_out23, demultiplexer_1_out24, demultiplexer_1_out25, demultiplexer_1_out26,
       demultiplexer_1_out27, demultiplexer_1_out28, demultiplexer_1_out29, demultiplexer_1_out30,
       demultiplexer_1_out31, WE10, WE11, WE12, WE13, WE14, WE15, WE16, WE17, WE18, WE19, WE20;
  wire [31:0] Q0, Q1, Q2, Q3, Q4, Q5, Q6, Q7, Q8, Q9, Q10, Q11, Q12, Q13, Q14, Q15, Q16, Q17, Q18, Q19, Q20,
       Q21, Q22, Q23, Q24, Q25, Q26, Q27, Q28, Q29, Q30, Q31;

  Demultiplexer #(.enable("false"), .select(5)) demultiplexer_1 (
    .out0(demultiplexer_1_out0), .out1(demultiplexer_1_out1), .out2(demultiplexer_1_out2),
    .out3(demultiplexer_1_out3), .out4(demultiplexer_1_out4), .out5(demultiplexer_1_out5),
    .out6(demultiplexer_1_out6), .out7(demultiplexer_1_out7), .out8(demultiplexer_1_out8),
    .out9(demultiplexer_1_out9), .out10(WE10), .out11(WE11), .out12(WE12), .out13(WE13), .out14(WE14),
    .out15(WE15), .out16(WE16), .out17(WE17), .out18(WE18), .out19(WE19), .out20(WE20),
    .out21(demultiplexer_1_out21), .out22(demultiplexer_1_out22), .out23(demultiplexer_1_out23),
    .out24(demultiplexer_1_out24), .out25(demultiplexer_1_out25), .out26(demultiplexer_1_out26),
    .out27(demultiplexer_1_out27), .out28(demultiplexer_1_out28), .out29(demultiplexer_1_out29),
    .out30(demultiplexer_1_out30), .out31(demultiplexer_1_out31), .in(Write), .sel(WReg));
  Register #(.width(32)) register_1 (.D(WData), .en(demultiplexer_1_out0), .clk(Clock_in), .Q(Q0), .clr(Write));
  Register #(.width(32)) register_2 (.D(WData), .en(demultiplexer_1_out1), .clk(Clock_in), .Q(Q1));  // open: clr
  Register #(.width(32)) register_3 (.D(WData), .en(demultiplexer_1_out2), .clk(Clock_in), .Q(Q2));  // open: clr
  Register #(.width(32)) register_4 (.D(WData), .en(demultiplexer_1_out3), .clk(Clock_in), .Q(Q3));  // open: clr
  Register #(.width(32)) register_5 (.D(WData), .en(demultiplexer_1_out4), .clk(Clock_in), .Q(Q4));  // open: clr
  Register #(.width(32)) register_6 (.D(WData), .en(demultiplexer_1_out5), .clk(Clock_in), .Q(Q5));  // open: clr
  Register #(.width(32)) register_7 (.D(WData), .en(demultiplexer_1_out6), .clk(Clock_in), .Q(Q6));  // open: clr
  Register #(.width(32)) register_8 (.D(WData), .en(demultiplexer_1_out7), .clk(Clock_in), .Q(Q7));  // open: clr
  Register #(.width(32)) register_9 (.D(WData), .en(demultiplexer_1_out8), .clk(Clock_in), .Q(Q8));  // open: clr
  Register #(.width(32)) register_10 (.D(WData), .en(demultiplexer_1_out9), .clk(Clock_in), .Q(Q9));  // open: clr
  Register #(.width(32)) register_11 (.D(WData), .en(WE10), .clk(Clock_in), .Q(Q10));  // open: clr
  Register #(.width(32)) register_12 (.D(WData), .en(WE11), .clk(Clock_in), .Q(Q11));  // open: clr
  Register #(.width(32)) register_13 (.D(WData), .en(WE12), .clk(Clock_in), .Q(Q12));  // open: clr
  Register #(.width(32)) register_14 (.D(WData), .en(WE13), .clk(Clock_in), .Q(Q13));  // open: clr
  Register #(.width(32)) register_15 (.D(WData), .en(WE14), .clk(Clock_in), .Q(Q14));  // open: clr
  Register #(.width(32)) register_16 (.D(WData), .en(WE15), .clk(Clock_in), .Q(Q15));  // open: clr
  Register #(.width(32)) register_17 (.D(WData), .en(WE16), .clk(Clock_in), .Q(Q16));  // open: clr
  Register #(.width(32)) register_18 (.D(WData), .en(WE17), .clk(Clock_in), .Q(Q17));  // open: clr
  Register #(.width(32)) register_19 (.D(WData), .en(WE18), .clk(Clock_in), .Q(Q18));  // open: clr
  Register #(.width(32)) register_20 (.D(WData), .en(WE19), .clk(Clock_in), .Q(Q19));  // open: clr
  Register #(.width(32)) register_21 (.D(WData), .en(WE20), .clk(Clock_in), .Q(Q20));  // open: clr
  Register #(.width(32)) register_22 (.D(WData), .en(demultiplexer_1_out21), .clk(Clock_in), .Q(Q21));  // open: clr
  Register #(.width(32)) register_23 (.D(WData), .en(demultiplexer_1_out22), .clk(Clock_in), .Q(Q22));  // open: clr
  Register #(.width(32)) register_24 (.D(WData), .en(demultiplexer_1_out23), .clk(Clock_in), .Q(Q23));  // open: clr
  Register #(.width(32)) register_25 (.D(WData), .en(demultiplexer_1_out24), .clk(Clock_in), .Q(Q24));  // open: clr
  Register #(.width(32)) register_26 (.D(WData), .en(demultiplexer_1_out25), .clk(Clock_in), .Q(Q25));  // open: clr
  Register #(.width(32)) register_27 (.D(WData), .en(demultiplexer_1_out26), .clk(Clock_in), .Q(Q26));  // open: clr
  Register #(.width(32)) register_28 (.D(WData), .en(demultiplexer_1_out27), .clk(Clock_in), .Q(Q27));  // open: clr
  Register #(.width(32)) register_29 (.D(WData), .en(demultiplexer_1_out28), .clk(Clock_in), .Q(Q28));  // open: clr
  Register #(.width(32)) register_30 (.D(WData), .en(demultiplexer_1_out29), .clk(Clock_in), .Q(Q29));  // open: clr
  Register #(.width(32)) register_31 (.D(WData), .en(demultiplexer_1_out30), .clk(Clock_in), .Q(Q30));  // open: clr
  Register #(.width(32)) register_32 (.D(WData), .en(demultiplexer_1_out31), .clk(Clock_in), .Q(Q31));  // open: clr
  Multiplexer #(.enable("false"), .select(5), .width(32)) multiplexer_1 (
    .in0(Q0), .in1(Q1), .in2(Q2), .in3(Q3), .in4(Q4), .in5(Q5), .in6(Q6), .in7(Q7), .in8(Q8), .in9(Q9),
    .in10(Q10), .in11(Q11), .in12(Q12), .in13(Q13), .in14(Q14), .in15(Q15), .in16(Q16), .in17(Q17),
    .in18(Q18), .in19(Q19), .in20(Q20), .in21(Q21), .in22(Q22), .in23(Q23), .in24(Q24), .in25(Q25),
    .in26(Q26), .in27(Q27), .in28(Q28), .in29(Q29), .in30(Q30), .in31(Q31), .out(RData1), .sel(RReg1));
  Multiplexer #(.enable("false"), .select(5), .width(32)) multiplexer_2 (
    .in0(Q0), .in1(Q1), .in2(Q2), .in3(Q3), .in4(Q4), .in5(Q5), .in6(Q6), .in7(Q7), .in8(Q8), .in9(Q9),
    .in10(Q10), .in11(Q11), .in12(Q12), .in13(Q13), .in14(Q14), .in15(Q15), .in16(Q16), .in17(Q17),
    .in18(Q18), .in19(Q19), .in20(Q20), .in21(Q21), .in22(Q22), .in23(Q23), .in24(Q24), .in25(Q25),
    .in26(Q26), .in27(Q27), .in28(Q28), .in29(Q29), .in30(Q30), .in31(Q31), .out(RData2), .sel(RReg2));
endmodule

module Datapath (
  input  [31:0] Instruction
);

  wire alu_ctrl_1_alu_src, clock_1_out;
  wire [3:0] alu_ctrl_1_alu_ctrl0;
  wire [31:0] bit_extender_1_out, multiplexer_1_out, register_file_1_rdata1, register_file_1_rdata2,
       thirtytwo_bit_alu_1_r;

  Clock clock_1 (.out(clock_1_out));
  assign bit_extender_1_out = {{20{Instruction[31]}}, Instruction[31:20]};  // Bit_Extender bit_extender_1
  Register_File register_file_1 (
    .RReg1(Instruction[19:15]), .WData(thirtytwo_bit_alu_1_r), .Clock_in(clock_1_out), .Write(1'b1),
    .WReg(Instruction[11:7]), .RReg2(Instruction[24:20]), .RData1(register_file_1_rdata1),
    .RData2(register_file_1_rdata2));
  ALU_Ctrl alu_ctrl_1 (
    .I30(Instruction[30]), .I14(Instruction[14]), .I13(Instruction[13]), .I12(Instruction[12]),
    .I6(Instruction[6]), .I5(Instruction[5]), .I4(Instruction[4]), .ALU_Ctrl3(alu_ctrl_1_alu_ctrl0[3]),
    .ALU_Ctrl2(alu_ctrl_1_alu_ctrl0[2]), .ALU_Ctrl1(alu_ctrl_1_alu_ctrl0[1]),
    .ALU_Ctrl0(alu_ctrl_1_alu_ctrl0[0]), .ALU_Src(alu_ctrl_1_alu_src));
  Multiplexer #(.enable("false"), .width(32)) multiplexer_1 (
    .in0(register_file_1_rdata2), .in1(bit_extender_1_out), .out(multiplexer_1_out), .sel(alu_ctrl_1_alu_src));
  ThirtyTwo_Bit_ALU thirtytwo_bit_alu_1 (
    .ALU_Ctrl(alu_ctrl_1_alu_ctrl0), .A(register_file_1_rdata1), .B(multiplexer_1_out),
    .R(thirtytwo_bit_alu_1_r));  // open: C_out
endmodule

module ImmGen (
  input  [31:0] Instruction,
  output [31:0] IMM32
);

  Multiplexer #(.enable("false"), .select(2)) multiplexer_1 (
    .in0(Instruction[20]), .in1(Instruction[7]), .in3(1'b0), .out(IMM32[0]), .sel(Instruction[6:5]));  // open: in2
  Multiplexer #(.enable("false"), .width(4)) multiplexer_2 (
    .in0(Instruction[24:21]), .in1(Instruction[11:8]), .out(IMM32[4:1]), .sel(Instruction[5]));
  Multiplexer #(.enable("false")) multiplexer_3 (
    .in0(Instruction[31]), .in1(Instruction[7]), .out(IMM32[11]), .sel(Instruction[6]));
  assign IMM32[31:12] = {{19{Instruction[31]}}, Instruction[31]};  // Bit_Extender bit_extender_1

  assign IMM32[10:5] = Instruction[30:25];

  // Other names for the same wires on the sheet: I30_25[5:0] = Instruction[30:25]; I5 = Instruction[5];
  //   I6_5[1:0] = Instruction[6:5]; I6 = Instruction[6]; I7 = Instruction[7]; I11_8[3:0] = Instruction[11:8];
  //   I20 = Instruction[20]; I24_21[3:0] = Instruction[24:21]; I31 = Instruction[31]
endmodule

module Instructional_Memory (
  input  [23:0] Address,
  input  Clk_In,
  output [31:0] Instruction
);

  wire not_1_out;

  not not_1 (not_1_out, Clk_In);
  RAM #(.addrWidth(22), .asyncread("true"), .dataWidth(32)) ram_1 (
    .addr(Address[23:2]), .we(1'b0), .oe(not_1_out), .dout(Instruction));  // open: clk, din
endmodule

module Data_Memory (
  input  [25:0] Address,
  input  Mem_Write,
  input  Mem_Read,
  input  Clk_In,
  input  [31:0] Write_Data,
  output [31:0] Read_Data
);

  RAM #(.addrWidth(24), .asyncread("true"), .dataWidth(32)) ram_1 (
    .addr(Address[25:2]), .we(Mem_Write), .oe(Mem_Read), .clk(Clk_In), .din(Write_Data), .dout(Read_Data));
endmodule

module Main_Control_Unit (
  input  I6,
  input  I5,
  input  I4,
  input  I3,
  input  I2,
  input  I1,
  input  I0,
  output MemtoReg,
  output RegWrite,
  output MemRead,
  output MemWrite,
  output Branch
);

  wire not_1_out, not_2_out;

  not not_1 (not_1_out, I6);
  not not_2 (not_2_out, I5);
  not not_3 (MemtoReg, I4);
  or or_1 (RegWrite, not_2_out, I4);
  and and_1 (MemRead, not_2_out, MemtoReg);
  and and_2 (MemWrite, not_1_out, I5, MemtoReg);

  assign Branch = I6;
endmodule
